# Fritzing sketch Grundaufbau_mit_LED (saved by Fritzing 0.9.3b)
breadboards: 1

parts:
  U1 = ESP32-Doit [part_number=ESP32-Doit]
  R1 = Resistor [tolerance=±1% resistance=47 package=THT]
  R2 = Resistor [tolerance=±1% resistance=47 package=THT]
  LED1 = RGB LED (com. cathode, rgb) [color="Red (633nm)" package="5 mm [THT]"]
  R3 = Resistor [tolerance=±1% resistance=47 package=THT]

nets:
  N1: U1.GPIO4, R2.Pin_0
  N2: U1.GPIO15, R3.Pin_0
  N3: U1.GNDr, LED1.green_anode
  N4: U1.GPIO16, R1.Pin_0
  N5: R1.Pin_1, LED1.red_anode
  N6: R2.Pin_1, LED1.common_cathode
  N7: LED1.blue_anode, R3.Pin_1

custom parts:
  ESP32-Doit: Doit ESP-WROOM-32 ESP32 ESP-32S Development Board 2.4GHz Dual-Mode WiFi + Bluetooth Dual Cores Microcontroller The ESP32 integrated with Antenna switches, RF Balun, power amplifiers, low-noise amplifiers, filters, and management modules, and the entire solution occupies the least area of PCB. 2.4 GHz Wi-Fi plus Bluetooth dual-mode chip, with TSMC Ultra-low power consumption 40nm technology,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
