# Fritzing sketch esp32_rfid_oled-Rgb-led (saved by Fritzing 0.9.3b)
breadboards: 1

parts:
  U1 = ESP32-Doit [part_number=ESP32-Doit]
  LED1 = RGB LED (com. anode, rbg) [package="5 mm [THT]"]  # not connected
  OLED_I2C1 = OLED 128x64 I2C Monochrome Display
  Bauteil1 = RFID-RC522-v3

nets:
  3V3: U1.3V3, OLED_I2C1.VDD, Bauteil1.3.3V
  N1: U1.GPIO5, Bauteil1.SDA
  N2: U1.GPIO18, Bauteil1.SCK
  N3: U1.GPIO19, Bauteil1.MISO
  N4: U1.GPIO21, OLED_I2C1.SDA
  N5: U1.GPIO22, OLED_I2C1.SCK
  N6: U1.GPIO23, Bauteil1.MOSI
  GND: U1.GNDr, OLED_I2C1.GND, Bauteil1.GND

custom parts:
  ESP32-Doit: Doit ESP-WROOM-32 ESP32 ESP-32S Development Board 2.4GHz Dual-Mode WiFi + Bluetooth Dual Cores Microcontroller The ESP32 integrated with Antenna switches, RF Balun, power amplifiers, low-noise amplifiers, filters, and management modules, and the entire solution occupies the least area of PCB. 2.4 GHz Wi-Fi plus Bluetooth dual-mode chip, with TSMC Ultra-low power consumption 40nm technology,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
  RFID-RC522-v3: A simple China made RFID-RC522 Reader (6x4 cm); do check the pin labels, as this is a MFRC522 based clone.
